# Fritzing sketch Arduino Kar (saved by Fritzing 0.9.3b)
breadboards: 1

parts:
  Componente1 = Arduino Uno (Rev3)
  M1 = DC Motor
  M2 = DC Motor
  M3 = DC Motor
  M4 = DC Motor
  IC1 = L293D [package=THT]
  Componente2 = Bluetooth HC-05 Macho

nets:
  N1: Componente1.D8, IC1.In_1
  N2: Componente1.D9_PWM, IC1.In_2
  N3: Componente1.D11_PWM/MOSI, IC1.Enable_1
  N4: Componente1.D12/MISO, IC1.Enable_2
  N5: Componente1.D0/RX, Componente2.TXD
  N6: Componente1.D1/TX, Componente2.RXD
  N7: Componente1.D6_PWM, IC1.In_3
  N8: Componente1.D7, M1.pin_2, M2.pin_2, IC1.In_4
  5V: Componente1.5V, IC1.+Vmotor, IC1.+V, Componente2.VCC
  GND: Componente1.GND, IC1.0V, Componente2.GND
  N9: M1.pin_1, M2.pin_1, IC1.Out_3_(_Controlled_by_Enable_2_)
  N10: M3.pin_1, M4.pin_1, IC1.Out_2_(_Controlled_by_Enable_1_)
  N11: M3.pin_2, M4.pin_2, IC1.Out_1_(_Controlled_by_Enable_1_)
